// Logisim project Part3_1230338_1230454_1230926-p3.circ as structural Verilog
module ALU (
  input  [31:0] Y,
  input  [31:0] Z,
  input  [3:0] ALUop,
  output [31:0] ALUres
);

  wire comparator_1_eq, comparator_1_lt;
  wire [31:0] adder_1_out, and_1_out, and_2_out, bitselector_1_out, bitselector_2_out, not_1_out, or_1_out,
       shifter_1_out, shifter_2_out, shifter_3_out, shifter_4_out, subtractor_1_out, xor_1_out;

  assign not_1_out = ~Y;  // NOT_Gate not_1, 32 bits wide
  Comparator #(.width(32)) comparator_1 (.a(Y), .b(Z), .eq(comparator_1_eq), .lt(comparator_1_lt));  // open: gt
  BitSelector #(.width(1), .group(32)) bitselector_1 (.in(comparator_1_eq), .out(bitselector_1_out), .sel(1'b0));
  BitSelector #(.width(1), .group(32)) bitselector_2 (.in(comparator_1_lt), .out(bitselector_2_out), .sel(1'b0));
  Shifter #(.width(32), .shift("ar")) shifter_1 (.in(Y), .\dist (Z[4:0]), .out(shifter_1_out));
  Shifter #(.width(32), .shift("lr")) shifter_2 (.in(Y), .\dist (Z[4:0]), .out(shifter_2_out));
  Shifter #(.width(32)) shifter_3 (.in(Y), .\dist (Z[4:0]), .out(shifter_3_out));
  Shifter #(.width(32), .shift("rr")) shifter_4 (.in(Y), .\dist (Z[4:0]), .out(shifter_4_out));
  assign xor_1_out = Y ^ Z;  // XOR_Gate xor_1, 32 bits wide
  assign and_1_out = Y & Z;  // AND_Gate and_1, 32 bits wide
  assign or_1_out = Y | Z;  // OR_Gate or_1, 32 bits wide
  assign and_2_out = not_1_out & Z;  // AND_Gate and_2, 32 bits wide
  Adder #(.width(32)) adder_1 (.a(Y), .b(Z), .out(adder_1_out), .cin(1'b0));  // open: cout
  Subtractor #(.width(32)) subtractor_1 (.a(Z), .b(Y), .out(subtractor_1_out), .bin(1'b0));  // open: bout
  Multiplexer #(.select(4), .width(32), .enable("false")) multiplexer_1 (
    .in0(xor_1_out), .in1(and_1_out), .in2(or_1_out), .in3(and_2_out), .in4(adder_1_out),
    .in5(bitselector_1_out), .in6(subtractor_1_out), .in7(bitselector_2_out), .in8(shifter_1_out),
    .in9(shifter_2_out), .in10(shifter_3_out), .in11(shifter_4_out), .out(ALUres), .sel(ALUop));  // open: in12, in13, in14, in15
endmodule

module RegFile (
  input  [3:0] Ry,
  input  [3:0] Rz,
  input  [31:0] BusX,
  input  [3:0] Rx,
  input  RegWrite,
  input  CLK,
  output [31:0] BusY,
  output [31:0] BusZ
);

  wire and_1_out, and_2_out, and_3_out, and_4_out, and_5_out, and_6_out, and_7_out, and_8_out, and_9_out,
       and_10_out, and_11_out, and_12_out, and_13_out, and_14_out, and_15_out, decoder_1_out0,
       decoder_2_out0, decoder_2_out1, decoder_2_out2, decoder_2_out3, decoder_2_out4, decoder_2_out5,
       decoder_2_out6, decoder_2_out7, decoder_2_out8, decoder_2_out9, decoder_2_out10, decoder_2_out11,
       decoder_2_out12, decoder_2_out13, decoder_2_out14, decoder_2_out15, decoder_3_out0, decoder_3_out1,
       decoder_3_out2, decoder_3_out3, decoder_3_out4, decoder_3_out5, decoder_3_out6, decoder_3_out7,
       decoder_3_out8, decoder_3_out9, decoder_3_out10, decoder_3_out11, decoder_3_out12, decoder_3_out13,
       decoder_3_out14, decoder_3_out15, r1, r2, r3, r4, r5, r6, r7, r8, r9, r10, r11, r12, r13, r14, r15;
  wire [31:0] R1_q, R2_q, R3_q, R4_q, R5_q, R6_q, R7_q, R8_q, R9_q, R10_q, R11_q, R12_q, R13_q, R14_q, R15_q;

  Decoder #(.select(4), .enable("false")) decoder_1 (
    .out0(decoder_1_out0), .out1(r1), .out2(r2), .out3(r3), .out4(r4), .out5(r5), .out6(r6), .out7(r7),
    .out8(r8), .out9(r9), .out10(r10), .out11(r11), .out12(r12), .out13(r13), .out14(r14), .out15(r15),
    .sel(Rx));
  and and_1 (and_1_out, r1, RegWrite);
  and and_2 (and_2_out, r2, RegWrite);
  and and_3 (and_3_out, r3, RegWrite);
  and and_4 (and_4_out, r4, RegWrite);
  and and_5 (and_5_out, r5, RegWrite);
  and and_6 (and_6_out, r6, RegWrite);
  and and_7 (and_7_out, r7, RegWrite);
  and and_8 (and_8_out, r8, RegWrite);
  and and_9 (and_9_out, r9, RegWrite);
  and and_10 (and_10_out, r10, RegWrite);
  and and_11 (and_11_out, r11, RegWrite);
  and and_12 (and_12_out, r12, RegWrite);
  and and_13 (and_13_out, r13, RegWrite);
  and and_14 (and_14_out, r14, RegWrite);
  and and_15 (and_15_out, r15, RegWrite);
  Register #(.width(32)) u_R1 (.D(BusX), .en(and_1_out), .Q(R1_q), .clk(CLK));  // open: clr
  Register #(.width(32)) u_R2 (.D(BusX), .en(and_2_out), .Q(R2_q), .clk(CLK));  // open: clr
  Register #(.width(32)) u_R3 (.D(BusX), .en(and_3_out), .Q(R3_q), .clk(CLK));  // open: clr
  Register #(.width(32)) u_R4 (.D(BusX), .en(and_4_out), .Q(R4_q), .clk(CLK));  // open: clr
  Register #(.width(32)) u_R5 (.D(BusX), .en(and_5_out), .Q(R5_q), .clk(CLK));  // open: clr
  Register #(.width(32)) u_R6 (.D(BusX), .en(and_6_out), .Q(R6_q), .clk(CLK));  // open: clr
  Register #(.width(32)) u_R7 (.D(BusX), .en(and_7_out), .Q(R7_q), .clk(CLK));  // open: clr
  Register #(.width(32)) u_R8 (.D(BusX), .en(and_8_out), .Q(R8_q), .clk(CLK));  // open: clr
  Register #(.width(32)) u_R9 (.D(BusX), .en(and_9_out), .Q(R9_q), .clk(CLK));  // open: clr
  Register #(.width(32)) u_R10 (.D(BusX), .en(and_10_out), .Q(R10_q), .clk(CLK));  // open: clr
  Register #(.width(32)) u_R11 (.D(BusX), .en(and_11_out), .Q(R11_q), .clk(CLK));  // open: clr
  Register #(.width(32)) u_R12 (.D(BusX), .en(and_12_out), .Q(R12_q), .clk(CLK));  // open: clr
  Register #(.width(32)) u_R13 (.D(BusX), .en(and_13_out), .Q(R13_q), .clk(CLK));  // open: clr
  Register #(.width(32)) u_R14 (.D(BusX), .en(and_14_out), .Q(R14_q), .clk(CLK));  // open: clr
  Register #(.width(32)) u_R15 (.D(BusX), .en(and_15_out), .Q(R15_q), .clk(CLK));  // open: clr
  assign BusY = decoder_2_out0 ? {32{1'b0}} : 32'bz;  // Controlled_Buffer controlled_buffer_1
  assign BusY = decoder_2_out1 ? R1_q : 32'bz;  // Controlled_Buffer controlled_buffer_2
  assign BusY = decoder_2_out2 ? R2_q : 32'bz;  // Controlled_Buffer controlled_buffer_3
  assign BusY = decoder_2_out3 ? R3_q : 32'bz;  // Controlled_Buffer controlled_buffer_4
  assign BusY = decoder_2_out4 ? R4_q : 32'bz;  // Controlled_Buffer controlled_buffer_5
  assign BusY = decoder_2_out5 ? R5_q : 32'bz;  // Controlled_Buffer controlled_buffer_6
  assign BusY = decoder_2_out6 ? R6_q : 32'bz;  // Controlled_Buffer controlled_buffer_7
  assign BusY = decoder_2_out7 ? R7_q : 32'bz;  // Controlled_Buffer controlled_buffer_8
  assign BusY = decoder_2_out8 ? R8_q : 32'bz;  // Controlled_Buffer controlled_buffer_9
  assign BusY = decoder_2_out9 ? R9_q : 32'bz;  // Controlled_Buffer controlled_buffer_10
  assign BusY = decoder_2_out10 ? R10_q : 32'bz;  // Controlled_Buffer controlled_buffer_11
  assign BusY = decoder_2_out11 ? R11_q : 32'bz;  // Controlled_Buffer controlled_buffer_12
  assign BusY = decoder_2_out12 ? R12_q : 32'bz;  // Controlled_Buffer controlled_buffer_13
  assign BusY = decoder_2_out13 ? R13_q : 32'bz;  // Controlled_Buffer controlled_buffer_14
  assign BusY = decoder_2_out14 ? R14_q : 32'bz;  // Controlled_Buffer controlled_buffer_15
  assign BusY = decoder_2_out15 ? R15_q : 32'bz;  // Controlled_Buffer controlled_buffer_16
  Decoder #(.select(4), .enable("false")) decoder_2 (
    .out0(decoder_2_out0), .out1(decoder_2_out1), .out2(decoder_2_out2), .out3(decoder_2_out3),
    .out4(decoder_2_out4), .out5(decoder_2_out5), .out6(decoder_2_out6), .out7(decoder_2_out7),
    .out8(decoder_2_out8), .out9(decoder_2_out9), .out10(decoder_2_out10), .out11(decoder_2_out11),
    .out12(decoder_2_out12), .out13(decoder_2_out13), .out14(decoder_2_out14), .out15(decoder_2_out15),
    .sel(Ry));
  assign BusZ = decoder_3_out0 ? {32{1'b0}} : 32'bz;  // Controlled_Buffer controlled_buffer_17
  assign BusZ = decoder_3_out1 ? R1_q : 32'bz;  // Controlled_Buffer controlled_buffer_18
  assign BusZ = decoder_3_out2 ? R2_q : 32'bz;  // Controlled_Buffer controlled_buffer_19
  assign BusZ = decoder_3_out3 ? R3_q : 32'bz;  // Controlled_Buffer controlled_buffer_20
  assign BusZ = decoder_3_out4 ? R4_q : 32'bz;  // Controlled_Buffer controlled_buffer_21
  assign BusZ = decoder_3_out5 ? R5_q : 32'bz;  // Controlled_Buffer controlled_buffer_22
  assign BusZ = decoder_3_out6 ? R6_q : 32'bz;  // Controlled_Buffer controlled_buffer_23
  assign BusZ = decoder_3_out7 ? R7_q : 32'bz;  // Controlled_Buffer controlled_buffer_24
  assign BusZ = decoder_3_out8 ? R8_q : 32'bz;  // Controlled_Buffer controlled_buffer_25
  assign BusZ = decoder_3_out9 ? R9_q : 32'bz;  // Controlled_Buffer controlled_buffer_26
  assign BusZ = decoder_3_out10 ? R10_q : 32'bz;  // Controlled_Buffer controlled_buffer_27
  assign BusZ = decoder_3_out11 ? R11_q : 32'bz;  // Controlled_Buffer controlled_buffer_28
  assign BusZ = decoder_3_out12 ? R12_q : 32'bz;  // Controlled_Buffer controlled_buffer_29
  assign BusZ = decoder_3_out13 ? R13_q : 32'bz;  // Controlled_Buffer controlled_buffer_30
  assign BusZ = decoder_3_out14 ? R14_q : 32'bz;  // Controlled_Buffer controlled_buffer_31
  assign BusZ = decoder_3_out15 ? R15_q : 32'bz;  // Controlled_Buffer controlled_buffer_32
  Decoder #(.select(4), .enable("false")) decoder_3 (
    .out0(decoder_3_out0), .out1(decoder_3_out1), .out2(decoder_3_out2), .out3(decoder_3_out3),
    .out4(decoder_3_out4), .out5(decoder_3_out5), .out6(decoder_3_out6), .out7(decoder_3_out7),
    .out8(decoder_3_out8), .out9(decoder_3_out9), .out10(decoder_3_out10), .out11(decoder_3_out11),
    .out12(decoder_3_out12), .out13(decoder_3_out13), .out14(decoder_3_out14), .out15(decoder_3_out15),
    .sel(Rz));
  // Probe on R1_q
  // Probe on R2_q
  // Probe on R3_q
  // Probe on R4_q
  // Probe on R5_q
  // Probe on R6_q
  // Probe on R7_q
  // Probe on R8_q
  // Probe on R9_q
  // Probe on R10_q
  // Probe on R11_q
  // Probe on R12_q
  // Probe on R13_q
  // Probe on R14_q
  // Probe on R15_q
endmodule

module Datapath (
);

  wire Bselect, CLK_out, Cond, ExtOP, MemRead, MemWrite, RegDest, RegWrite;
  wire [1:0] updatePC, Wdata;
  wire [3:0] ALUOP, multiplexer_1_out, Rz;
  wire [7:0] Imm8, OP, shifter_1_out;
  wire [15:0] shifter_2_out;
  wire [15:8] Imm16;
  wire [19:0] adder_2_out, adder_3_out, adder_4_out, bit_extender_1_out, bit_extender_4_out,
       bit_extender_5_out, multiplexer_5_out, newPC, PC, PC___1;
  wire [31:0] alu_1_alures, bit_extender_6_out, multiplexer_2_out, multiplexer_3_out, ram_1_data, SextImm8,
       x, y, Z, ZextImm8;

  Clock CLK (.out(CLK_out));
  Register #(.width(20)) u_PC (.D(newPC), .en(1'b1), .Q(PC), .clk(CLK_out));  // open: clr
  Adder #(.width(20)) adder_1 (.a(PC), .b(20'h1), .out(PC___1));  // open: cin, cout
  Cond cond_1 (.Rz(Z), .Ry(y), .Cond(Cond), .op(OP));
  PC pc_2 (.op(OP), .updatePC(updatePC));
  ROM #(.addrWidth(20), .dataWidth(24)) rom_1 (.addr(PC), .data({OP, Imm16, Imm8}));  // open: sel
  Multiplexer #(.width(4), .enable("false")) multiplexer_1 (
    .in0(Imm16[15:12]), .in1(4'b1111), .out(multiplexer_1_out), .sel(RegDest));
  Control_Unit control_unit_1 (
    .Opcode(OP[4:0]), .MemRead(MemRead), .MemWrite(MemWrite), .Bselect(Bselect), .RegWrite(RegWrite),
    .RegDest(RegDest), .Wdata(Wdata), .AluOp(ALUOP), .Extop(ExtOP));
  RegFile regfile_1 (
    .Ry(Imm16[11:8]), .Rz(Rz), .BusX(x), .Rx(multiplexer_1_out), .RegWrite(RegWrite), .CLK(CLK_out),
    .BusY(y), .BusZ(Z));
  assign bit_extender_1_out = {{12{Imm8[7]}}, Imm8};  // Bit_Extender bit_extender_1
  assign ZextImm8 = {{24{1'b0}}, Imm8};  // Bit_Extender bit_extender_2
  assign SextImm8 = {{24{Imm8[7]}}, Imm8};  // Bit_Extender bit_extender_3
  Multiplexer #(.width(32), .enable("false")) multiplexer_2 (
    .in0(Z), .in1(multiplexer_3_out), .out(multiplexer_2_out), .sel(Bselect));
  Multiplexer #(.width(32), .enable("false")) multiplexer_3 (
    .in0(ZextImm8), .in1(SextImm8), .out(multiplexer_3_out), .sel(ExtOP));
  Adder #(.width(20)) adder_2 (.a(bit_extender_1_out), .b(y[19:0]), .out(adder_2_out));  // open: cin, cout
  Multiplexer #(.select(5), .width(4), .enable("false")) multiplexer_4 (
    .in0(Imm8[7:4]), .in1(Imm8[7:4]), .in2(Imm8[7:4]), .in3(Imm8[7:4]), .in4(Imm8[7:4]), .in5(Imm8[7:4]),
    .in6(Imm8[7:4]), .in7(Imm8[7:4]), .in8(Imm8[7:4]), .in9(Imm8[7:4]), .in10(Imm8[7:4]), .in11(Imm8[7:4]),
    .in12(Imm8[7:4]), .in13(Imm8[7:4]), .in14(Imm8[7:4]), .in15(Imm8[7:4]), .in16(Imm8[7:4]),
    .in17(Imm8[7:4]), .in18(Imm8[7:4]), .in19(Imm8[7:4]), .in20(Imm16[15:12]), .in21(Imm16[15:12]),
    .in22(Imm16[15:12]), .in23(Imm16[15:12]), .in24(Imm8[7:4]), .in25(Imm16[15:12]), .in26(Imm8[7:4]),
    .in27(Imm8[7:4]), .in28(Imm8[7:4]), .in29(Imm8[7:4]), .in30(Imm8[7:4]), .in31(Imm8[7:4]), .out(Rz),
    .sel(OP[4:0]));
  ALU alu_1 (.Y(y), .Z(multiplexer_2_out), .ALUres(alu_1_alures), .ALUop(ALUOP));
  Shifter shifter_1 (.in(Imm8), .\dist (3'b001), .out(shifter_1_out));
  assign bit_extender_4_out = {{12{shifter_1_out[7]}}, shifter_1_out};  // Bit_Extender bit_extender_4
  Shifter #(.width(16)) shifter_2 (.in({Imm16, Imm8}), .\dist (4'b0001), .out(shifter_2_out));
  Adder #(.width(20)) adder_3 (.a(PC), .b(bit_extender_4_out), .out(adder_3_out), .cin(1'b0));  // open: cout
  assign bit_extender_5_out = {{4{shifter_2_out[15]}}, shifter_2_out};  // Bit_Extender bit_extender_5
  RAM #(.addrWidth(20), .dataWidth(32), .bus("separate")) ram_1 (
    .addr(adder_2_out), .din(Z), .data(ram_1_data), .str(MemWrite), .clk(CLK_out), .ld(MemRead));  // open: sel, clr
  assign bit_extender_6_out = {{12{1'b0}}, PC___1};  // Bit_Extender bit_extender_6
  Multiplexer #(.width(20), .enable("false")) multiplexer_5 (
    .in0(PC___1), .in1(adder_3_out), .out(multiplexer_5_out), .sel(Cond));
  Multiplexer #(.select(2), .width(32), .enable("false")) multiplexer_6 (
    .in0(alu_1_alures), .in1(ram_1_data), .in2(bit_extender_6_out), .out(x), .sel(Wdata));  // open: in3
  Adder #(.width(20)) adder_4 (.a(PC), .b(bit_extender_5_out), .out(adder_4_out), .cin(1'b0));  // open: cout
  Multiplexer #(.select(2), .width(20), .enable("false")) multiplexer_7 (
    .in0(PC___1), .in1(multiplexer_5_out), .in2(adder_4_out), .out(newPC), .sel(updatePC));  // open: in3

  // Other names for the same wires on the sheet: Ry[3:0] = Imm16[11:8]; Rx[3:0] = Imm16[15:12]; Imm16[7:0] = Imm8;
  //   z_t[3:0] = Imm8[7:4]

  // Notes on the sheet:
  //   contents of rom_1 (hex, n*v repeats v):
  //   182101 183102 1230 14130 24130 35130 45420 54650 64120 74160 885fc 94177 a94a8 b9976 cc511 dbc22
  //   103503 117308 12a707 13c507 147c03 157c04 167c05 177c04 0 0 1230 0 0 21230 11230 1a0001 0 1b0002 0 0
  //   0 19c603 c1003 c2000 142102 c2201 1affff
endmodule

module Cond (
  input  [31:0] Rz,
  input  [31:0] Ry,
  input  [7:0] op,
  output Cond
);

  wire comparator_1_gt, EQ, GTE, LT, NEQ;

  Comparator #(.width(32)) comparator_1 (.a(Rz), .b(Ry), .gt(comparator_1_gt), .eq(EQ), .lt(LT));
  or or_1 (GTE, comparator_1_gt, EQ);
  not not_1 (NEQ, EQ);
  Multiplexer #(.select(5), .enable("false")) multiplexer_1 (
    .in0(1'b0), .in1(1'b0), .in2(1'b0), .in3(1'b0), .in4(1'b0), .in5(1'b0), .in6(1'b0), .in7(1'b0),
    .in8(1'b0), .in9(1'b0), .in10(1'b0), .in11(1'b0), .in12(1'b0), .in13(1'b0), .in14(1'b0), .in15(1'b0),
    .in16(1'b0), .in17(1'b0), .in18(1'b0), .in19(1'b0), .in20(EQ), .in21(NEQ), .in22(LT), .in23(GTE),
    .in24(1'b0), .in25(1'b0), .in26(1'b0), .in27(1'b0), .in28(1'b0), .in29(1'b0), .in30(1'b0), .in31(1'b0),
    .out(Cond), .sel(op[4:0]));
endmodule

module PC (
  input  [7:0] op,
  output [1:0] updatePC
);

  Multiplexer #(.select(5), .width(2), .enable("false")) multiplexer_1 (
    .in0(2'b00), .in1(2'b00), .in2(2'b00), .in3(2'b00), .in4(2'b00), .in5(2'b00), .in6(2'b00), .in7(2'b00),
    .in8(2'b00), .in9(2'b00), .in10(2'b00), .in11(2'b00), .in12(2'b00), .in13(2'b00), .in14(2'b00),
    .in15(2'b00), .in16(2'b00), .in17(2'b00), .in18(2'b00), .in19(2'b00), .in20(2'b01), .in21(2'b01),
    .in22(2'b01), .in23(2'b01), .in24(2'b00), .in25(2'b00), .in26(2'b10), .in27(2'b10), .in28(2'b00),
    .in29(2'b00), .in30(2'b00), .in31(2'b00), .out(updatePC), .sel(op[4:0]));
endmodule

module Control_Unit (
  input  [4:0] Opcode,
  output [3:0] AluOp,
  output [1:0] Wdata,
  output RegDest,
  output RegWrite,
  output Extop,
  output Bselect,
  output MemWrite,
  output MemRead
);

  ROM #(.addrWidth(5), .dataWidth(12)) rom_1 (
    .addr(Opcode), .data({MemRead, MemWrite, Bselect, Extop, RegWrite, RegDest, Wdata, AluOp}));  // open: sel

  // Notes on the sheet:
  //   contents of rom_1 (hex, n*v repeats v):
  //   81 83 82 80 84 86 85 87 381 383 382 380 384 386 385 387 38a 389 388 38b f 1f 1f 1f 89f 51f 3f ef
endmodule
